# Fritzing sketch RaspberyPi ClampForLamp Circuit Scheme (saved by Fritzing 0.9.3b)
breadboards: 1

parts:
  Parça1 = Breakout Board for Electret Microphone
  U1 = RELAY [package=relay-jzc]
  Raspberry_Pi1 = Raspberry Pi 2

nets:
  VCC: Parça1.VCC, Raspberry_Pi1.3v3
  GND: Parça1.GND, U1.NC, Raspberry_Pi1.GND
  N1: Parça1.AUD, Raspberry_Pi1.GPIO4
  N2: U1.COIL2, Raspberry_Pi1.5V
  N3: U1.NO, Raspberry_Pi1.GPIO17
